# Fritzing sketch PCB (saved by Fritzing 0.9.3b)
breadboards: 3

parts:
  Raspberry_Pi_1 = Raspberry Pi 3 [part_number=RPI-3-V1.2]
  LED1 = LED - 5mm [color="Red (633nm)" package="5 mm [THT]"]
  LED2 = LED - 5mm [color="Red (633nm)" package="5 mm [THT]"]
  RHT1 = Humidity and Temperature Sensor RHT03
  Part1 = Photon
  RHT2 = Humidity and Temperature Sensor RHT03
  U1 = RELAY [package=relay-t9a-2]

nets:
  N1: Raspberry_Pi_1.GND, LED1.cathode, LED2.cathode, RHT1.GND_2
  N2: Raspberry_Pi_1.GPIO17, RHT1.Data-signal
  N3: Raspberry_Pi_1.GPIO22, U1.NO
  5V: Raspberry_Pi_1.5V, RHT1.Vcc
  N4: LED1.anode, U1.COIL1
  N5: LED2.anode, U1.COIL2
  N6: Part1.GND, RHT2.GND_2
  N7: Part1.D2, RHT2.Data-signal
  3V3: Part1.3V3, RHT2.Vcc
